// Logisim project logi.circ as structural Verilog: 1 circuit, main circuit main
module main (
);

  wire A_IN, A_OUT, adder_2_cout, ADDER_OUT, ALU_0, ALU_1, ALU_2, ALU_3, and_7_out, and_8_out, and_9_out,
       and_10_out, and_11_out, and_12_out, and_14_out, and_15_out, AND_OUT, B_IN, B_OUT, button_1_out,
       button_2_out, C_OUT, CARRY, CLEAR, CLK, controlled_buffer_9_out, controlled_buffer_18_out,
       counter_2_carry, counter_4_carry, decoder_1_out1, FLAGS_IN, HIGH, IGNB, INST_IN, MAR_IN, MAR_UP, MIH,
       MIL, nor_2_out, nor_3_out, not_1_out, not_2_out, not_3_out, not_4_out, not_5_out, not_6_out,
       not_7_out, not_8_out, OI, OO, or_1_out, or_4_out, or_5_out, OR_OUT, PIH, PIL, POH, POL, PROGRAM_IN,
       PROGRAM_OUT, PROGRAM_UP, RAM_IN, RAM_OUT, RESET, RI, RO, ROMO, SHL, SHR, SP_IN, SP_NOT, SP_OUT, SUB,
       XOR_OUT;
  wire [1:0] FLG, or_7_out;
  wire [3:0] counter_1_q, counter_3_q, R15;
  wire [6:0] controlled_buffer_3_out, keyboard_1_data, keyboard_2_data, register_1_q;
  wire [6:6] controlled_buffer_3_out_2;
  wire [7:0] adder_1_out, adder_2_out, and_13_out, bit_extender_1_out, controlled_buffer_1_out,
       controlled_buffer_8_out, controlled_buffer_14_out, counter_2_q, counter_4_q, counter_5_q, or_6_out,
       register_2_q, register_3_q, register_4_q, register_5_q, rom_3_data, xor_1_out, xor_2_out;

  Button button_1 (.out(button_1_out));
  not not_1 (not_1_out, CLK);
  Counter #(.max('hf), .width(4)) counter_1 (
    .clr(or_1_out), .clk(not_1_out), .Q(counter_1_q));  // open: load, up, count, D, carry
  or or_1 (or_1_out, RESET, button_1_out, CLEAR);
  not not_2 (not_2_out, HIGH);
  Register #(.width(7)) register_1 (
    .D(controlled_buffer_3_out), .en(INST_IN), .clk(CLK), .Q(register_1_q), .clr(CLEAR));
  and and_1 (MIL, MAR_IN, not_2_out);
  and and_2 (MIH, MAR_IN, HIGH);
  and and_3 (POL, PROGRAM_OUT, not_2_out);
  and and_4 (PIL, PROGRAM_IN, not_2_out);
  and and_5 (POH, PROGRAM_OUT, HIGH);
  and and_6 (PIH, PROGRAM_IN, HIGH);
  Decoder #(.select(4)) decoder_1 (
    .out1(decoder_1_out1), .out2(AND_OUT), .out3(OR_OUT), .out4(XOR_OUT), .out5(SUB), .out6(SP_OUT),
    .out7(B_OUT), .out8(A_OUT), .out9(RAM_OUT), .out10(PROGRAM_OUT), .out11(CARRY), .out12(C_OUT),
    .out13(SHL), .out14(SHR), .out15(IGNB), .sel({ALU_3, ALU_2, ALU_1, ALU_0}), .en(1'b1));  // open: out0
  ROM #(.addrWidth(13)) rom_1 (
    .addr({FLG, register_1_q, counter_1_q}), .data({ALU_3, ALU_2, ALU_1, ALU_0, HIGH, SP_IN, B_IN, A_IN}));
  ROM #(.addrWidth(13)) rom_2 (
    .addr({FLG, register_1_q, counter_1_q}),
    .data({SP_NOT, MAR_UP, MAR_IN, RAM_IN, INST_IN, PROGRAM_UP, PROGRAM_IN, RESET}));
  or or_2 (ADDER_OUT, SUB, SUB, CARRY, IGNB);
  or or_3 (FLAGS_IN, ADDER_OUT, SHL, XOR_OUT, IGNB, OR_OUT, AND_OUT, SHR);
  // Probe on adder_1_out
  assign controlled_buffer_1_out = SP_NOT ? 8'h1 : 8'bz;  // Controlled_Buffer controlled_buffer_1
  not not_3 (not_3_out, SP_NOT);
  assign controlled_buffer_1_out = not_3_out ? {8{1'b1}} : 8'bz;  // Controlled_Buffer controlled_buffer_2
  Register register_2 (.D(adder_1_out), .en(SP_IN), .clk(CLK), .Q(register_2_q), .clr(CLEAR));
  and and_7 (and_7_out, SP_NOT, not_4_out);
  not not_4 (not_4_out, SP_IN);
  Adder adder_1 (.a(controlled_buffer_1_out), .b(register_2_q), .out(adder_1_out), .cin(1'b0));  // open: cout
  assign {controlled_buffer_3_out_2[6], controlled_buffer_3_out} = and_8_out ? register_2_q : 8'bz;  // Controlled_Buffer controlled_buffer_3
  and and_8 (and_8_out, SP_OUT, not_5_out);
  and and_9 (and_9_out, SP_OUT, HIGH);
  not not_5 (not_5_out, HIGH);
  Register register_3 (
    .D({controlled_buffer_3_out_2[6], controlled_buffer_3_out}), .en(and_7_out), .clk(CLK), .Q(register_3_q),
    .clr(CLEAR));
  // Probe on {controlled_buffer_3_out_2[6], controlled_buffer_3_out}
  assign {controlled_buffer_3_out_2[6], controlled_buffer_3_out} = and_9_out ? {8{1'b1}} : 8'bz;  // Controlled_Buffer controlled_buffer_4
  assign {controlled_buffer_3_out_2[6], controlled_buffer_3_out} = C_OUT ? register_3_q : 8'bz;  // Controlled_Buffer controlled_buffer_5
  and and_10 (and_10_out, counter_4_carry, PROGRAM_UP);
  assign {controlled_buffer_3_out_2[6], controlled_buffer_3_out} = B_OUT ? controlled_buffer_8_out : 8'bz;  // Controlled_Buffer controlled_buffer_6
  assign {controlled_buffer_3_out_2[6], controlled_buffer_3_out} = A_OUT ? register_4_q : 8'bz;  // Controlled_Buffer controlled_buffer_7
  Register register_4 (
    .D({controlled_buffer_3_out_2[6], controlled_buffer_3_out}), .en(A_IN), .clk(CLK), .Q(register_4_q),
    .clr(CLEAR));
  Register register_5 (
    .D({controlled_buffer_3_out_2[6], controlled_buffer_3_out}), .en(B_IN), .clk(CLK), .Q(register_5_q),
    .clr(CLEAR));
  Counter counter_2 (
    .clr(CLEAR), .load(MIL), .count(MAR_UP), .clk(CLK),
    .D({controlled_buffer_3_out_2[6], controlled_buffer_3_out}), .carry(counter_2_carry), .Q(counter_2_q));  // open: up
  and and_11 (and_11_out, MAR_UP, counter_2_carry);
  Counter counter_3 (
    .clr(CLEAR), .load(MIH), .count(and_11_out), .clk(CLK),
    .D({controlled_buffer_3_out_2[6], controlled_buffer_3_out}), .Q({R15, counter_3_q}));  // open: up, carry
  Counter counter_4 (
    .clr(CLEAR), .load(PIL), .count(PROGRAM_UP), .clk(CLK),
    .D({controlled_buffer_3_out_2[6], controlled_buffer_3_out}), .carry(counter_4_carry), .Q(counter_4_q));  // open: up
  Counter counter_5 (
    .clr(CLEAR), .load(PIH), .count(and_10_out), .clk(CLK),
    .D({controlled_buffer_3_out_2[6], controlled_buffer_3_out}), .Q(counter_5_q));  // open: up, carry
  assign controlled_buffer_8_out = not_6_out ? register_5_q : 8'bz;  // Controlled_Buffer controlled_buffer_8
  not not_6 (not_6_out, IGNB);
  Button button_2 (.out(button_2_out));
  assign controlled_buffer_9_out = not_7_out ? IGNB : 1'bz;  // Controlled_Buffer controlled_buffer_9
  assign xor_1_out = controlled_buffer_8_out ^ bit_extender_1_out;  // XOR_Gate xor_1, 8 bits wide
  assign bit_extender_1_out = {{7{SUB}}, SUB};  // Bit_Extender bit_extender_1
  Pull_Resistor pull_resistor_1 (.node(controlled_buffer_8_out));
  Keyboard keyboard_1 (.clk(button_2_out), .re(1'b1), .data(keyboard_1_data));  // open: clr, avail
  assign {controlled_buffer_3_out_2[6], controlled_buffer_3_out} = POL ? counter_4_q : 8'bz;  // Controlled_Buffer controlled_buffer_10
  assign {controlled_buffer_3_out_2[6], controlled_buffer_3_out} = POH ? counter_5_q : 8'bz;  // Controlled_Buffer controlled_buffer_11
  not not_7 (not_7_out, CARRY);
  assign controlled_buffer_9_out = CARRY ? FLG[0] : 1'bz;  // Controlled_Buffer controlled_buffer_12
  or or_4 (or_4_out, controlled_buffer_9_out, SUB);
  Adder adder_2 (.a(xor_1_out), .b(register_4_q), .out(adder_2_out), .cin(or_4_out), .cout(adder_2_cout));
  or or_5 (or_5_out, ADDER_OUT, SUB);
  assign {controlled_buffer_3_out_2[6], controlled_buffer_3_out} = ADDER_OUT ? adder_2_out : 8'bz;  // Controlled_Buffer controlled_buffer_13
  and and_12 (and_12_out, adder_2_cout, or_5_out);
  assign controlled_buffer_14_out = RAM_IN ? {controlled_buffer_3_out_2[6], controlled_buffer_3_out} : 8'bz;  // Controlled_Buffer controlled_buffer_14
  assign {controlled_buffer_3_out_2[6], controlled_buffer_3_out} = RAM_OUT ? controlled_buffer_14_out : 8'bz;  // Controlled_Buffer controlled_buffer_15
  assign and_13_out = register_4_q & controlled_buffer_8_out;  // AND_Gate and_13, 8 bits wide
  assign {controlled_buffer_3_out_2[6], controlled_buffer_3_out} = AND_OUT ? and_13_out : 8'bz;  // Controlled_Buffer controlled_buffer_16
  RAM #(.addrWidth(16), .asyncread("true"), .databus("bidir")) ram_1 (
    .addr({R15, counter_3_q, counter_2_q}), .we(RI), .oe(RO), .clk(CLK), .data(controlled_buffer_14_out));
  ROM #(.addrWidth(16)) rom_3 (.addr({R15, counter_3_q, counter_2_q}), .data(rom_3_data));
  // Probe on keyboard_1_data
  assign or_6_out = register_4_q | controlled_buffer_8_out;  // OR_Gate or_6, 8 bits wide
  assign {controlled_buffer_3_out_2[6], controlled_buffer_3_out} = OR_OUT ? or_6_out : 8'bz;  // Controlled_Buffer controlled_buffer_17
  Keyboard keyboard_2 (.clk(CLK), .re(OO), .clr(CLEAR), .data(keyboard_2_data));  // open: avail
  Pull_Resistor pull_resistor_2 (.node({controlled_buffer_3_out_2[6], controlled_buffer_3_out}));
  assign xor_2_out = register_4_q ^ controlled_buffer_8_out;  // XOR_Gate xor_2, 8 bits wide
  assign controlled_buffer_18_out = SHR ? register_4_q[0] : 1'bz;  // Controlled_Buffer controlled_buffer_18
  assign {controlled_buffer_3_out_2[6], controlled_buffer_3_out} = XOR_OUT ? xor_2_out : 8'bz;  // Controlled_Buffer controlled_buffer_19
  assign controlled_buffer_18_out = SHL ? register_4_q[7] : 1'bz;  // Controlled_Buffer controlled_buffer_20
  assign controlled_buffer_14_out = ROMO ? rom_3_data : 8'bz;  // Controlled_Buffer controlled_buffer_21
  Pull_Resistor pull_resistor_3 (.node(controlled_buffer_18_out));
  or or_7 (or_7_out[0], controlled_buffer_18_out, and_12_out);
  Button button_3 (.out(CLEAR));
  Clock clock_1 (.out(CLK));
  Pull_Resistor pull_resistor_4 (.node(controlled_buffer_14_out[7]));
  assign controlled_buffer_14_out[6:0] = OO ? keyboard_2_data : 7'bz;  // Controlled_Buffer controlled_buffer_22
  nor nor_1 (or_7_out[1], controlled_buffer_3_out[0], controlled_buffer_3_out[1], controlled_buffer_3_out[2], controlled_buffer_3_out[3], controlled_buffer_3_out[4], controlled_buffer_3_out[5], controlled_buffer_3_out[6], controlled_buffer_3_out_2[6]);
  assign controlled_buffer_3_out = SHR ? register_4_q[7:1] : 7'bz;  // Controlled_Buffer controlled_buffer_23
  assign {controlled_buffer_3_out_2[6], controlled_buffer_3_out[6:1]} = SHL ? register_4_q[6:0] : 7'bz;  // Controlled_Buffer controlled_buffer_24
  Register #(.width(2)) register_6 (.D(or_7_out), .en(FLAGS_IN), .clk(CLK), .Q(FLG), .clr(CLEAR));
  nor nor_2 (nor_2_out, R15[3], R15[2]);
  TTY #(.cols(60), .rows(20)) tty_1 (.data(controlled_buffer_14_out[6:0]), .clk(CLK), .we(OI), .clr(CLEAR));
  and and_14 (and_14_out, nor_2_out, R15[1]);
  and and_15 (and_15_out, nor_2_out, not_8_out);
  not not_8 (not_8_out, R15[1]);
  nor nor_3 (nor_3_out, and_14_out, and_15_out);
  and and_16 (RO, RAM_OUT, nor_3_out);
  and and_17 (RI, RAM_IN, nor_3_out);
  and and_18 (ROMO, RAM_OUT, and_15_out);
  and and_19 (OI, RAM_IN, and_14_out);
  and and_20 (OO, RAM_OUT, and_14_out);

  // Notes on the sheet:
  //   contents of rom_1 (hex, n*v repeats v):
  //   a0 a8 90 13*0 a0 a8 90 91 12*0 a0 a8 90 90 98 c0 91 9*0 a0 a8 90 90 98 c0 90 98 c0 91 6*0 a0 a8 90
  //   92 12*0 a0 a8 90 90 98 c0 92 9*0 a0 a8 90 90 98 c0 90 98 c0 92 6*0 a0 a8 90 90 98 c0 80 9*0 a0 a8 90
  //   90 98 c0 90 98 c0 80 6*0 a0 a8 90 90 98 c0 70 9*0 a0 a8 90 90 98 c0 90 98 c0 70 6*0 a0 a8 90 82 12*0
  //   a0 a8 90 71 12*0 a0 a8 90 69 12*0 a0 a8 90 61 12*0 a0 a8 90 6a 12*0 a0 a8 90 62 12*0 a0 a8 90 80 78
  //   91 10*0 a0 a8 90 80 78 92 10*0 a0 a8 90 90 98 c0 10 9*0 a0 a8 90 92 11 11*0 a0 a8 90 90 98 c0 92 11
  //   8*0 a0 a8 90 90 98 c0 90 98 c0 92 11 5*0 a0 a8 90 11 12*0 a0 a8 90 91 12 11*0 a0 a8 90 90 98 c0 91
  //   12 8*0 a0 a8 90 90 98 c0 90 98 c0 91 12 5*0 a0 a8 90 12 12*0 a0 a8 90 90 98 c0 b0 9*0 a0 a8 90 92 b1
  //   11*0 a0 a8 90 90 98 c0 92 b1 8*0 a0 a8 90 90 98 c0 90 98 c0 92 b1 5*0 a0 a8 90 b1 12*0 a0 a8 90 91
  //   b2 11*0 a0 a8 90 90 98 c0 91 b2 8*0 a0 a8 90 90 98 c0 90 98 c0 91 b2 5*0 a0 a8 90 b2 12*0 a0 a8 90
  //   90 98 c0 50 9*0 a0 a8 90 92 51 11*0 a0 a8 90 90 98 c0 92 51 8*0 a0 a8 90 90 98 c0 90 98 c0 92 51 5*0
  //   a0 a8 90 51 12*0 a0 a8 90 91 52 11*0 a0 a8 90 90 98 c0 91 52 8*0 a0 a8 90 90 98 c0 90 98 c0 91 52
  //   5*0 a0 a8 90 52 12*0 a0 a8 90 90 98 c0 20 9*0 a0 a8 90 92 21 11*0 a0 a8 90 90 98 c0 92 21 8*0 a0 a8
  //   90 90 98 c0 90 98 c0 92 21 5*0 a0 a8 90 21 12*0 a0 a8 90 91 22 11*0 a0 a8 90 90 98 c0 91 22 8*0 a0
  //   a8 90 90 98 c0 90 98 c0 91 22 5*0 a0 a8 90 22 12*0 a0 a8 90 90 98 c0 30 9*0 a0 a8 90 92 31 11*0 a0
  //   a8 90 90 98 c0 92 31 8*0 a0 a8 90 90 98 c0 90 98 c0 91 31 5*0 a0 a8 90 31 12*0 a0 a8 90 91 32 11*0
  //   a0 a8 90 90 98 c0 91 32 8*0 a0 a8 90 90 98 c0 90 98 c0 91 32 5*0 a0 a8 90 32 12*0 a0 a8 90 90 98 c0
  //   40 9*0 a0 a8 90 92 41 11*0 a0 a8 90 90 98 c0 92 41 8*0 a0 a8 90 90 98 c0 90 98 c0 91 41 5*0 a0 a8 90
  //   41 12*0 a0 a8 90 91 42 11*0 a0 a8 90 90 98 c0 91 42 8*0 a0 a8 90 90 98 c0 90 98 c0 91 42 5*0 a0 a8
  //   90 42 12*0 a0 a8 90 90 98 c0 d1 d1 d1 d0 6*0 a0 a8 90 90 98 c0 92 4*d1 5*0 a0 a8 90 4*d1 9*0 a0 a8
  //   90 90 98 c0 d1 d0 8*0 a0 a8 90 90 98 c0 92 d1 d1 7*0 a0 a8 90 d1 d1 11*0 a0 a8 90 90 98 c0 d0 9*0 a0
  //   a8 90 90 98 c0 92 d1 8*0 a0 a8 90 d1 12*0 a0 a8 90 90 98 c0 e1 e1 e1 e0 6*0 a0 a8 90 90 98 c0 92
  //   4*e1 5*0 a0 a8 90 4*e1 9*0 a0 a8 90 90 98 c0 e1 e0 8*0 a0 a8 90 90 98 c0 92 e1 e1 7*0 a0 a8 90 e1 e1
  //   11*0 a0 a8 90 90 98 c0 e0 9*0 a0 a8 90 90 98 c0 92 e1 8*0 a0 a8 90 e1 12*0 a0 a8 90 92 50 11*0 a0 a8
  //   90 90 98 c0 92 50 8*0 a0 a8 90 90 98 c0 90 98 c0 92 50 5*0 a0 a8 90 91 50 11*0 a0 a8 90 90 98 c0 91
  //   50 8*0 a0 a8 90 90 98 c0 90 98 c0 91 50 5*0 a0 a8 90 50 12*0 a0 a8 90 90 98 c0 10*0 a0 a8 90 90 98
  //   c0 90 98 c0 7*0 a0 a8 90 90 98 c0 90 98 c0 90 98 c0 4*0 a0 a8 90 13*0 a0 a8 90 13*0 a0 a8 90 13*0 a0
  //   a8 90 13*0 a0 a8 90 13*0 a0 a8 90 13*0 a0 a8 90 90 98 c0 10*0 a0 a8 90 90 98 c0 90 98 c0 7*0 a0 a8
  //   90 90 98 c0 90 98 c0 90 98 c0 4*0 a0 a8 90 90 98 c0 10*0 a0 a8 90 90 98 c0 90 98 c0 7*0 a0 a8 90 90
  //   98 c0 90 98 c0 90 98 c0 4*0 a0 a8 90 4 6c 60 a0 0 a8 a8 a0 90 98 c0 0 0 a0 a8 90 13*0 a0 a8 90 4 6c
  //   60 a0 0 a8 a8 a0 90 98 c0 0 0 a0 a8 90 13*0 a0 a8 90 4 6c 60 a0 0 a8 a8 a0 90 98 c0 0 0 a0 a8 90 60
  //   68 90 0 98 4 4 6*0 a0 a8 90 4 60 68 80 9*0 a0 a8 90 4 60 68 70 9*0 a0 a8 90 4 60 68 60 9*0 a0 a8 90
  //   60 68 91 4 9*0 a0 a8 90 60 68 92 4 73*0 a0 a8 90 13*0 a0 a8 90 91 12*0 a0 a8 90 90 98 c0 91 9*0 a0
  //   a8 90 90 98 c0 90 98 c0 91 6*0 a0 a8 90 92 12*0 a0 a8 90 90 98 c0 92 9*0 a0 a8 90 90 98 c0 90 98 c0
  //   92 6*0 a0 a8 90 90 98 c0 80 9*0 a0 a8 90 90 98 c0 90 98 c0 80 6*0 a0 a8 90 90 98 c0 70 9*0 a0 a8 90
  //   90 98 c0 90 98 c0 70 6*0 a0 a8 90 82 12*0 a0 a8 90 71 12*0 a0 a8 90 69 12*0 a0 a8 90 61 12*0 a0 a8
  //   90 6a 12*0 a0 a8 90 62 12*0 a0 a8 90 80 78 91 10*0 a0 a8 90 80 78 92 10*0 a0 a8 90 90 98 c0 10 9*0
  //   a0 a8 90 92 11 11*0 a0 a8 90 90 98 c0 92 11 8*0 a0 a8 90 90 98 c0 90 98 c0 92 11 5*0 a0 a8 90 11
  //   12*0 a0 a8 90 91 12 11*0 a0 a8 90 90 98 c0 91 12 8*0 a0 a8 90 90 98 c0 90 98 c0 91 12 5*0 a0 a8 90
  //   12 12*0 a0 a8 90 90 98 c0 b0 9*0 a0 a8 90 92 b1 11*0 a0 a8 90 90 98 c0 92 b1 8*0 a0 a8 90 90 98 c0
  //   90 98 c0 92 b1 5*0 a0 a8 90 b1 12*0 a0 a8 90 91 b2 11*0 a0 a8 90 90 98 c0 91 b2 8*0 a0 a8 90 90 98
  //   c0 90 98 c0 91 b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
  //   contents of rom_2 (hex, n*v repeats v):
  //   20 20 4c 13*1 20 20 4c 4 12*1 20 20 4c c4 24 20 0 9*1 20 20 4c c4 24 20 c0 20 20 0 6*1 20 20 4c 4
  //   12*1 20 20 4c c4 24 20 0 9*1 20 20 4c c4 24 20 c0 20 20 0 6*1 20 20 4c c4 24 20 10 9*1 20 20 4c c4
  //   24 20 c0 20 20 10 6*1 20 20 4c c4 24 20 10 9*1 20 20 4c c4 24 20 c0 20 20 10 6*1 20 20 4c 0 12*1 20
  //   20 4c 0 12*1 20 20 4c 0 12*1 20 20 4c 0 12*1 20 20 4c 0 12*1 20 20 4c 0 12*1 20 20 4c 20 20 0 10*1
  //   20 20 4c 20 20 0 10*1 20 20 4c c4 24 20 10 9*1 20 20 4c 4 0 11*1 20 20 4c c4 24 20 0 0 8*1 20 20 4c
  //   c4 24 20 c0 20 20 0 0 5*1 20 20 4c 0 12*1 20 20 4c 4 0 11*1 20 20 4c c4 24 20 0 0 8*1 20 20 4c c4 24
  //   20 c0 20 20 0 0 5*1 20 20 4c 0 12*1 20 20 4c c4 24 20 10 9*1 20 20 4c 4 0 11*1 20 20 4c c4 24 20 0 0
  //   8*1 20 20 4c c4 24 20 c0 20 20 0 0 5*1 20 20 4c 0 12*1 20 20 4c 4 0 11*1 20 20 4c c4 24 20 0 0 8*1
  //   20 20 4c c4 24 20 c0 20 20 0 0 5*1 20 20 4c 0 12*1 20 20 4c c4 24 20 10 9*1 20 20 4c 4 0 11*1 20 20
  //   4c c4 24 20 0 0 8*1 20 20 4c c4 24 20 c0 20 20 0 0 5*1 20 20 4c 0 12*1 20 20 4c 4 0 11*1 20 20 4c c4
  //   24 20 0 0 8*1 20 20 4c c4 24 20 c0 20 20 0 0 5*1 20 20 4c 0 12*1 20 20 4c c4 24 20 10 9*1 20 20 4c 4
  //   0 11*1 20 20 4c c4 24 20 0 0 8*1 20 20 4c c4 24 20 c0 20 20 0 0 5*1 20 20 4c 0 12*1 20 20 4c 4 0
  //   11*1 20 20 4c c4 24 20 0 0 8*1 20 20 4c c4 24 20 c0 20 20 0 0 5*1 20 20 4c 0 12*1 20 20 4c c4 24 20
  //   10 9*1 20 20 4c 4 0 11*1 20 20 4c c4 24 20 0 0 8*1 20 20 4c c4 24 20 c0 20 20 0 0 5*1 20 20 4c 0
  //   12*1 20 20 4c 4 0 11*1 20 20 4c c4 24 20 0 0 8*1 20 20 4c c4 24 20 c0 20 20 0 0 5*1 20 20 4c 0 12*1
  //   20 20 4c c4 24 20 10 9*1 20 20 4c 4 0 11*1 20 20 4c c4 24 20 0 0 8*1 20 20 4c c4 24 20 c0 20 20 0 0
  //   5*1 20 20 4c 0 12*1 20 20 4c 4 0 11*1 20 20 4c c4 24 20 0 0 8*1 20 20 4c c4 24 20 c0 20 20 0 0 5*1
  //   20 20 4c 0 12*1 20 20 4c c4 24 20 0 0 0 10 6*1 20 20 4c c4 24 20 5*0 5*1 20 20 4c 4*0 9*1 20 20 4c
  //   c4 24 20 0 10 8*1 20 20 4c c4 24 20 0 0 0 7*1 20 20 4c 0 0 11*1 20 20 4c c4 24 20 10 9*1 20 20 4c c4
  //   24 20 0 0 8*1 20 20 4c 0 12*1 20 20 4c c4 24 20 0 0 0 10 6*1 20 20 4c c4 24 20 5*0 5*1 20 20 4c 4*0
  //   9*1 20 20 4c c4 24 20 0 10 8*1 20 20 4c c4 24 20 0 0 0 7*1 20 20 4c 0 0 11*1 20 20 4c c4 24 20 10
  //   9*1 20 20 4c c4 24 20 0 0 8*1 20 20 4c 0 12*1 20 20 4c 4 0 11*1 20 20 4c c4 24 20 0 0 8*1 20 20 4c
  //   c4 24 20 c0 20 20 0 0 5*1 20 20 4c 4 0 11*1 20 20 4c c4 24 20 0 0 8*1 20 20 4c c4 24 20 c0 20 20 0 0
  //   5*1 20 20 4c 0 12*1 20 20 4c c4 6 2 10*1 20 20 4c c4 24 20 c0 2 2 7*1 20 20 4c c4 24 20 c0 20 20 c0
  //   2 2 4*1 20 20 4c 44 44 11*1 20 20 4c 44 44 11*1 20 20 4c 44 44 11*1 20 20 4c 44 44 11*1 20 20 4c 44
  //   44 11*1 20 20 4c 44 44 11*1 20 20 4c c4 6 2 10*1 20 20 4c c4 24 20 c0 2 2 7*1 20 20 4c c4 24 20 c0
  //   20 20 c0 2 2 4*1 20 20 4c c4 6 2 10*1 20 20 4c c4 24 20 c0 2 2 7*1 20 20 4c c4 24 20 c0 20 20 c0 2 2
  //   4*1 20 20 4c 0 20 20 10 40 10 20 20 c4 6 2 1 1 20 20 4c 44 44 11*1 20 20 4c 0 20 20 10 40 10 20 20
  //   c4 6 2 1 1 20 20 4c 44 44 11*1 20 20 4c 0 20 20 10 40 10 20 20 c4 6 2 1 1 20 20 4c 20 20 2 40 2 80
  //   80 4 4 4*1 20 20 4c 0 20 20 10 9*1 20 20 4c 0 20 20 10 9*1 20 20 4c 0 20 20 10 9*1 20 20 4c 20 20 0
  //   80 9*1 20 20 4c 20 20 0 80 9*1 64*0 20 20 4c 13*1 20 20 4c 4 12*1 20 20 4c c4 24 20 0 9*1 20 20 4c
  //   c4 24 20 c0 20 20 0 6*1 20 20 4c 4 12*1 20 20 4c c4 24 20 0 9*1 20 20 4c c4 24 20 c0 20 20 0 6*1 20
  //   20 4c c4 24 20 10 9*1 20 20 4c c4 24 20 c0 20 20 10 6*1 20 20 4c c4 24 20 10 9*1 20 20 4c c4 24 20
  //   c0 20 20 10 6*1 20 20 4c 0 12*1 20 20 4c 0 12*1 20 20 4c 0 12*1 20 20 4c 0 12*1 20 20 4c 0 12*1 20
  //   20 4c 0 12*1 20 20 4c 20 20 0 10*1 20 20 4c 20 20 0 10*1 20 20 4c c4 24 20 10 9*1 20 20 4c 4 0 11*1
  //   20 20 4c c4 24 20 0 0 8*1 20 20 4c c4 24 20 c0 20 20 0 0 5*1 20 20 4c 0 12*1 20 20 4c 4 0 11*1 20 20
  //   4c c4 24 20 0 0 8*1 20 20 4c c4 24 20 c0 20 20 0 0 5*1 20 20 4c 0 12*1 20 20 4c c4 24 20 10 9*1 20
  //   20 4c 4 0 11*1 20 20 4c c4 24 20 0 0 8*1 20 20 4c c4 24 20 c0 20 20 0 0 5*1 20 20 4c 0 12*1 20 20 4c
  //   4 0 11*1 20 20 4c c4 24 20 0 0 8*1 20 20 4c c4 24 20 c0 20 20 0 0 5*1 20 20 4c 0 12*1 20 20 4c c4 24
  //   20 10 9*1 20 20 4c 4 0 11*1 20 20 4c c4 24 20 0 0 8*1 20 20 4c c4 24 20 c0 20 20 0 0 5*1 20 20 4c 0
  //   12*1 20 20 4c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
  //   contents of rom_3 (hex, n*v repeats v):
  //   1 5c 7 0 20 1 22 4 2 71 4 2 1 a 7 0 20 71 17 0 62 33 0 1 20 4 80 7 22 2 9 23 2 1 0 7 0 80 7 1 80 7 2
  //   80 7 3 80 7 a 80 76 2 0 20 5b 0 6e 3e 0 62 33 0 7 0 20 8 22 2 5b a 72 17 0 68 57 0 2 22 2 14 1 7 22
  //   2 62 33 0 3 22 2 5b 0 6e 62 0 62 57 0 5b a 68 2 1 5b 52 68 8b 0 5b 3a 68 a8 0 5b 2e 77 72 8e 0 7a 71
  //   7c 1 5b 0 73 97 1 2 22 2 14 1 7 22 2 62 57 0 63 0 80 1 1 7 a 80 2 0 80 7 2 80 2 1 80 7 3 80 1 0 7 0
  //   80 7 1 80 76 1 2 7 a 80 2 0 80 7 2 80 2 1 80 7 3 80 1 0 7 0 80 7 1 80 2 22 2 14 1 7 22 2 3 22 2 5b a
  //   68 c 0 5b 20 68 e1 0 71 7c 1 5b 0 73 97 1 62 c1 0 2 0 80 8 2 80 2 2 80 14 1 7 2 80 2 3 80 1d 0 7 3
  //   80 1 0 7 0 80 7 1 80 62 c1 0 2 a 80 5b 0 72 12 1 5b 1 72 2a 1 62 c 0 2 1 80 71 dd 1 2 0 80 71 dd 1 1
  //   3a 7 0 20 3 0 80 71 dd 1 76 71 65 1 1 20 7 0 20 3 2 80 71 dd 1 2 2 80 14 1 7 2 80 2 3 80 1d 0 7 3 80
  //   5c 1 80 68 59 1 2 2 80 2f f 72 65 1 62 2d 1 2 2 80 5c 0 80 68 20 2 62 2d 1 1 a 7 0 20 2 3 80 71 dd 1
  //   2 2 80 71 dd 1 1 3a 7 0 20 76 5b 30 6b 94 1 5b 3a 6b 93 1 5b 41 6b 94 1 5b 47 6b 93 1 62 94 1 76 1 0
  //   76 3 22 2 5b 40 74 b6 1 26 30 7 6 80 4 4 9 9 80 71 b9 1 2 6 80 5 0 80 37 0 80 76 26 7 76 2 1 80 51 7
  //   1 80 2 0 80 51 7 0 80 2 1 80 1d 0 7 1 80 2 9 80 26 1 7 9 80 68 20 2 62 b9 1 7 4 80 2f f 5b a 74 1 2
  //   14 30 7 5 80 2 4 80 54 5b a 74 1 2 14 30 7 0 20 2 5 80 7 0 20 76 14 7 76 7 22 2 9 23 2 3 22 2 5b 0
  //   68 20 2 7 0 20 2 22 2 14 1 7 22 2 62 a 2 76 76 20 4d 6f 6e 69 74 6f 72 20 a 20 30 78 34 30 30 30 20
  //   2d 20 42 41 53 49 43 20 a
endmodule
